// Logisim project final_circuit.circ as structural Verilog
module main (
);

  wire clock_1_out, system_bus_1_buttons_e, system_bus_1_display_e, system_bus_1_ram_m;
  wire [2:0] system_bus_1_ram_ctrl;
  wire [3:0] stalwart_cpu_1_mar_o, system_bus_1_ram_a;
  wire [5:0] stalwart_cpu_1_ext_ctrl;
  wire [6:0] display_handler_1_x1, display_handler_1_x10, display_handler_1_x100;
  wire [7:0] button_handler_1_o, ram_16x8_1_data_out, system_bus_1_cpu_d_o, system_bus_1_display;
  wire [9:0] button_7_out;

  Button button_1 (.out(button_7_out[1]));
  Button button_2 (.out(button_7_out[2]));
  Button button_3 (.out(button_7_out[4]));
  Button button_4 (.out(button_7_out[5]));
  Button button_5 (.out(button_7_out[7]));
  Button button_6 (.out(button_7_out[8]));
  Button button_7 (.out(button_7_out[0]));
  Clock clock_1 (.out(clock_1_out));
  ROM #(.addrWidth(4)) rom_1 ();  // open: addr, data
  Button button_8 (.out(button_7_out[3]));
  Button button_9 (.out(button_7_out[6]));
  Button button_10 (.out(button_7_out[9]));
  Button_Handler button_handler_1 (.O(button_handler_1_o), .I(button_7_out), .CS(system_bus_1_buttons_e));
  RAM_16x8 ram_16x8_1 (
    .Data_out(ram_16x8_1_data_out), .Mode(system_bus_1_ram_m), .CLK(clock_1_out),
    .CPU_CTRL(system_bus_1_ram_ctrl), .Address(system_bus_1_ram_a));  // open: Data_in
  System_Bus system_bus_1 (
    .RAM_M(system_bus_1_ram_m), .Display_E(system_bus_1_display_e), .Buttons(button_handler_1_o),
    .CPU_CTRL(stalwart_cpu_1_ext_ctrl), .RAM_D_O(ram_16x8_1_data_out), .Display(system_bus_1_display),
    .CPU_D_I(system_bus_1_cpu_d_o), .CPU_D_O(system_bus_1_cpu_d_o), .RAM_D_I(ram_16x8_1_data_out),
    .RAM_A(system_bus_1_ram_a), .CPU_A_I(stalwart_cpu_1_mar_o), .Buttons_E(system_bus_1_buttons_e),
    .RAM_CTRL(system_bus_1_ram_ctrl));
  Stalwart_CPU stalwart_cpu_1 (
    .MBR_O(system_bus_1_cpu_d_o), .MAR_O(stalwart_cpu_1_mar_o), .CLK(clock_1_out),
    .MBR_I(system_bus_1_cpu_d_o), .EXT_CTRL(stalwart_cpu_1_ext_ctrl));
  _7_Segment_Display u_7_segment_display_1 (
    .g(display_handler_1_x100[0]), .f(display_handler_1_x100[1]), .a(display_handler_1_x100[2]),
    .b(display_handler_1_x100[3]), .e(display_handler_1_x100[6]), .d(display_handler_1_x100[5]),
    .c(display_handler_1_x100[4]));  // open: dp
  Display_Handler display_handler_1 (
    .x1(display_handler_1_x1), .IE(system_bus_1_display_e), .x100(display_handler_1_x100),
    .I(system_bus_1_display), .x10(display_handler_1_x10));
  _7_Segment_Display u_7_segment_display_2 (
    .g(display_handler_1_x10[0]), .f(display_handler_1_x10[1]), .a(display_handler_1_x10[2]),
    .b(display_handler_1_x10[3]), .e(display_handler_1_x10[6]), .d(display_handler_1_x10[5]),
    .c(display_handler_1_x10[4]));  // open: dp
  _7_Segment_Display u_7_segment_display_3 (
    .g(display_handler_1_x1[0]), .f(display_handler_1_x1[1]), .a(display_handler_1_x1[2]),
    .b(display_handler_1_x1[3]), .e(display_handler_1_x1[6]), .d(display_handler_1_x1[5]),
    .c(display_handler_1_x1[4]));  // open: dp

  // Notes on the sheet:
  //   contents of rom_1 (hex, n*v repeats v):
  //   4e 5d 34 3c 9a 6e 4f 1c 24 6f b0 4f 10 1
endmodule

module Button_Handler (
  input  [9:0] I,
  input  CS,
  output [7:0] O
);

  wire controlled_buffer_1_out, not_1_out, or_5_out;
  wire [3:0] byte_reg_1_o, or_3_out;
  wire [7:4] byte_reg_1_o_2;

  or or_1 (or_3_out[3], I[9], I[8]);
  or or_2 (or_3_out[2], I[7], I[6], I[5], I[4]);
  or or_3 (or_3_out[0], I[9], I[7], I[5], I[3], I[1]);
  or or_4 (or_3_out[1], I[7], I[6], I[3], I[2]);
  or or_5 (or_5_out, I[0], or_3_out[3], or_3_out[2], or_3_out[1], or_3_out[0]);
  assign controlled_buffer_1_out = not_1_out ? or_5_out : 1'bz;  // Controlled_Buffer controlled_buffer_1
  not not_1 (not_1_out, CS);
  Byte_Reg byte_reg_1 (
    .Chip_Select(1'b1), .I({byte_reg_1_o, or_3_out}), .Clock(controlled_buffer_1_out),
    .O({byte_reg_1_o_2, byte_reg_1_o}), .Mode_RW(controlled_buffer_1_out));
  assign O = CS ? {byte_reg_1_o_2, byte_reg_1_o} : 8'bz;  // Controlled_Buffer controlled_buffer_2
endmodule

module Display_Handler (
  input  [7:0] I,
  input  IE,
  output [6:0] x100,
  output [6:0] x10,
  output [6:0] x1
);

  wire controlled_buffer_1_out, or_1_out;
  wire [3:0] binary_to_bcd_1_binary1, binary_to_bcd_1_binary10, binary_to_bcd_1_binary100;
  wire [7:0] byte_reg_1_o;

  or or_1 (or_1_out, I[0], I[1], I[2], I[3], I[4], I[5], I[6], I[7]);
  assign controlled_buffer_1_out = IE ? or_1_out : 1'bz;  // Controlled_Buffer controlled_buffer_1
  Byte_Reg byte_reg_1 (
    .Chip_Select(1'b1), .I(I), .Clock(controlled_buffer_1_out), .O(byte_reg_1_o),
    .Mode_RW(controlled_buffer_1_out));
  Binary_to_BCD binary_to_bcd_1 (
    .BInaryInput(byte_reg_1_o), .Binary1(binary_to_bcd_1_binary1), .Binary10(binary_to_bcd_1_binary10),
    .Binary100(binary_to_bcd_1_binary100));
  BCD_to_7Segment bcd_to_7segment_1 (.out_2(x100), .in_1(binary_to_bcd_1_binary1));
  BCD_to_7Segment bcd_to_7segment_2 (.out_2(x10), .in_1(binary_to_bcd_1_binary10));
  BCD_to_7Segment bcd_to_7segment_3 (.out_2(x1), .in_1(binary_to_bcd_1_binary100));
  _7_Segment_Display u_7_segment_display_1 (
    .g(x100[0]), .f(x100[1]), .a(x100[2]), .b(x100[3]), .e(x100[6]), .d(x100[5]), .c(x100[4]));  // open: dp
  _7_Segment_Display u_7_segment_display_2 (
    .g(x10[0]), .f(x10[1]), .a(x10[2]), .b(x10[3]), .e(x10[6]), .d(x10[5]), .c(x10[4]));  // open: dp
  _7_Segment_Display u_7_segment_display_3 (
    .g(x1[0]), .f(x1[1]), .a(x1[2]), .b(x1[3]), .e(x1[6]), .d(x1[5]), .c(x1[4]));  // open: dp

  // Notes on the sheet:
  //   Segment order: GFABCDE
endmodule

module System_Bus (
  input  [3:0] CPU_A_I,
  input  [7:0] CPU_D_I,
  input  [7:0] RAM_D_I,
  input  [7:0] Buttons,
  input  [5:0] CPU_CTRL,
  output [3:0] RAM_A,
  output [7:0] CPU_D_O,
  output [7:0] RAM_D_O,
  output [7:0] Display,
  output [2:0] RAM_CTRL,
  output RAM_M,
  output Buttons_E,
  output Display_E
);

  wire or_1_out, or_2_out;
  wire [7:0] controlled_buffer_1_out;

  or or_1 (or_1_out, CPU_CTRL[0], CPU_CTRL[5]);
  assign controlled_buffer_1_out = or_1_out ? CPU_D_I : 8'bz;  // Controlled_Buffer controlled_buffer_1
  assign RAM_A = CPU_CTRL[0] ? CPU_A_I : 4'bz;  // Controlled_Buffer controlled_buffer_2
  assign CPU_D_O = or_2_out ? controlled_buffer_1_out : 8'bz;  // Controlled_Buffer controlled_buffer_3
  or or_2 (or_2_out, CPU_CTRL[2], CPU_CTRL[4]);
  assign controlled_buffer_1_out = CPU_CTRL[2] ? RAM_D_I : 8'bz;  // Controlled_Buffer controlled_buffer_4
  assign RAM_D_O = CPU_CTRL[0] ? controlled_buffer_1_out : 8'bz;  // Controlled_Buffer controlled_buffer_5
  assign controlled_buffer_1_out = CPU_CTRL[4] ? Buttons : 8'bz;  // Controlled_Buffer controlled_buffer_6
  assign Display = CPU_CTRL[5] ? controlled_buffer_1_out : 8'bz;  // Controlled_Buffer controlled_buffer_7

  assign Buttons_E = CPU_CTRL[4];
  assign Display_E = CPU_CTRL[5];
  assign RAM_CTRL = CPU_CTRL[2:0];
  assign RAM_M = CPU_CTRL[3];

  // Notes on the sheet:
  //   Address bus: 4 bits
  //   Data bus: 8 bits
  //   Control Bus: Set size as required
endmodule

module Stalwart_CPU (
  input  [7:0] MBR_I,
  input  CLK,
  output [3:0] MAR_O,
  output [7:0] MBR_O,
  output [5:0] EXT_CTRL
);

  wire control_unit_1_alu_add_sub, control_unit_1_d0_cs, control_unit_1_d0_rw, control_unit_1_d1_cs,
       control_unit_1_d1_rw, control_unit_1_ir_cs, control_unit_1_ir_rw, control_unit_1_mar_cs,
       control_unit_1_mar_rw, control_unit_1_mbr_cs, control_unit_1_mbr_rw;
  wire [2:0] alu_1_status, control_unit_1_ic_ctrl;
  wire [3:0] buffer_1_out, control_unit_1_alu_ctrl;
  wire [7:0] IR_o;
  wire [7:4] buffer_1_out_2;

  Nibble_Reg MAR (
    .O(MAR_O), .Chip_Select(control_unit_1_mar_cs), .Mode_RW(control_unit_1_mar_rw), .Clock(CLK),
    .I(buffer_1_out));
  Byte_Reg MBR (
    .Chip_Select(control_unit_1_mbr_cs), .I(MBR_I), .Clock(CLK), .O(MBR_O), .Mode_RW(control_unit_1_mbr_rw));
  Byte_Reg D0 (.Chip_Select(control_unit_1_d0_cs), .I(MBR_O), .Clock(CLK), .O(MBR_O), .Mode_RW(control_unit_1_d0_rw));
  Byte_Reg D1 (.Chip_Select(control_unit_1_d1_cs), .I(MBR_O), .Clock(CLK), .O(MBR_O), .Mode_RW(control_unit_1_d1_rw));
  // Probe on buffer_1_out
  assign {buffer_1_out_2, buffer_1_out} = MBR_O;  // Buffer buffer_1, 8 bits wide
  // Probe on MBR_O
  ALU alu_1 (
    .Status(alu_1_status), .A(MBR_O), .R(MBR_O), .L(MBR_O), .ADD_SUB(control_unit_1_alu_add_sub), .CLK(CLK),
    .CTRL(control_unit_1_alu_ctrl));
  Nibble_Counter IC (
    .O(buffer_1_out), .Write_Enable(control_unit_1_ic_ctrl[0]), .Clock(CLK),
    .Read_Enable(control_unit_1_ic_ctrl[1]), .Increment(control_unit_1_ic_ctrl[2]));  // open: I
  Byte_Reg IR (.Chip_Select(control_unit_1_ir_cs), .I(MBR_O), .Clock(CLK), .O(IR_o), .Mode_RW(control_unit_1_ir_rw));
  Control_Unit control_unit_1 (
    .OP(IR_o), .D0_CS(control_unit_1_d0_cs), .D0_RW(control_unit_1_d0_rw), .D1_CS(control_unit_1_d1_cs),
    .D1_RW(control_unit_1_d1_rw), .ALU_CTRL(control_unit_1_alu_ctrl),
    .ALU_ADD_SUB(control_unit_1_alu_add_sub), .IC_CTRL(control_unit_1_ic_ctrl),
    .MAR_RW(control_unit_1_mar_rw), .MAR_CS(control_unit_1_mar_cs), .MBR_RW(control_unit_1_mbr_rw),
    .MBR_CS(control_unit_1_mbr_cs), .IR_RW(control_unit_1_ir_rw), .IR_CS(control_unit_1_ir_cs), .CLK(CLK),
    .RAM_SEND(EXT_CTRL[0]), .RAM_EXEC(EXT_CTRL[1]), .RAM_FETCH(EXT_CTRL[2]), .RAM_MODE(EXT_CTRL[3]),
    .INPUT_ENABLE(EXT_CTRL[4]), .OUTPUT_ENABLE(EXT_CTRL[5]), .ALU_FLAGS(alu_1_status));
endmodule

module Control_Unit (
  input  [2:0] ALU_FLAGS,
  input  [7:0] OP,
  input  CLK,
  output D0_RW,
  output D0_CS,
  output D1_RW,
  output D1_CS,
  output ALU_ADD_SUB,
  output [3:0] ALU_CTRL,
  output [2:0] IC_CTRL,
  output MAR_RW,
  output MAR_CS,
  output MBR_RW,
  output MBR_CS,
  output IR_RW,
  output INPUT_ENABLE,
  output IR_CS,
  output OUTPUT_ENABLE,
  output RAM_SEND,
  output RAM_EXEC,
  output RAM_FETCH,
  output RAM_MODE
);

  wire A4a_out, A4b_out, ADD_out, ALU_out, BEQ_out, BNQ_out, INP_out, iR2_out, LD_out, M_S_out, MATH_out,
       MRa_out, MRb_out, or_1_out, or_2_out, or_3_out, or_4_out, or_5_out, or_6_out, or_7_out, or_8_out,
       or_9_out, or_10_out, PRT_out, R2a_out, R2b_out, RCa_out, RCb_out, RMa_out, RMb_out, STR_out, SUB_out;
  wire [3:0] t_ff_6_q;

  // AND_Gate R1R has open pins: in0=t_ff_6_q[0], in1=LD_out, out=open
  and R2a (R2a_out, t_ff_6_q[1], LD_out);
  // AND_Gate R3 has open pins: in0=t_ff_6_q[2], in1=LD_out, out=open
  and MRa (MRa_out, t_ff_6_q[3], LD_out);
  // OR_Gate iMR has open pins: in0=MRa_out, in1=MRb_out, out=open
  or iR2 (iR2_out, R2a_out, R2b_out);
  and LD (LD_out, ~OP[7], OP[6], ~OP[5]);  // AND_Gate
  and STR (STR_out, ~OP[7], OP[6], OP[5]);  // AND_Gate
  and RMa (RMa_out, t_ff_6_q[0], STR_out);
  // AND_Gate R1W has open pins: in0=t_ff_6_q[1], in1=STR_out, out=open
  and R2b (R2b_out, t_ff_6_q[2], STR_out);
  // OR_Gate iRM has open pins: in0=RMa_out, in1=RMb_out, out=open
  or or_1 (or_1_out, t_ff_6_q[3], IC_CTRL[1]);
  T_Flip_Flop #(.trigger("falling")) t_ff_1 (.T(or_1_out), .clk(CLK), .Q(IC_CTRL[1]));  // open: Qn, reset, preset
  and PRT (PRT_out, ~OP[7], ~OP[6], ~OP[5], OP[4], ~OP[3]);  // AND_Gate
  and RMb (RMb_out, t_ff_6_q[0], PRT_out);
  and O_C (OUTPUT_ENABLE, t_ff_6_q[1], PRT_out);
  or or_2 (or_2_out, IC_CTRL[1], RAM_SEND);
  T_Flip_Flop #(.trigger("falling")) t_ff_2 (.T(or_2_out), .clk(CLK), .Q(RAM_SEND));  // open: Qn, reset, preset
  and INP (INP_out, ~OP[7], ~OP[6], ~OP[5], OP[4], OP[3]);  // AND_Gate
  and I_C (INPUT_ENABLE, t_ff_6_q[2], INP_out);
  and MRb (MRb_out, t_ff_6_q[3], INP_out);
  not not_1 (RAM_MODE, RAM_SEND);
  or or_3 (or_3_out, RAM_SEND, IC_CTRL[2]);
  T_Flip_Flop #(.trigger("falling")) t_ff_3 (.T(or_3_out), .clk(CLK), .Q(IC_CTRL[2]));  // open: Qn, reset, preset
  and ADD (ADD_out, ~OP[7], ~OP[6], OP[5], ~OP[4]);  // AND_Gate
  and A4a (A4a_out, t_ff_6_q[3], ADD_out);
  // OR_Gate iA4 has open pins: in0=A4a_out, in1=A4b_out, out=open
  or or_4 (or_4_out, IC_CTRL[2], MBR_RW);
  T_Flip_Flop #(.trigger("falling")) t_ff_4 (.T(or_4_out), .clk(CLK), .Q(MBR_RW));  // open: Qn, reset, preset
  and SUB (SUB_out, ~OP[7], ~OP[6], OP[5], OP[4]);  // AND_Gate
  and A4b (A4b_out, t_ff_6_q[3], SUB_out);
  or or_5 (or_5_out, MBR_RW, IR_RW);
  T_Flip_Flop #(.trigger("falling")) t_ff_5 (.T(or_5_out), .clk(CLK), .Q(IR_RW));  // open: Qn, reset, preset
  and BNQ (BNQ_out, OP[7], OP[6]);
  and RCa (RCa_out, t_ff_6_q[3], BNQ_out);
  // OR_Gate iRC has open pins: in0=RCa_out, in1=RCb_out, out=open
  or or_6 (or_6_out, IR_RW, t_ff_6_q[0]);
  T_Flip_Flop #(.trigger("falling")) t_ff_6 (.T(or_6_out), .clk(CLK), .Q(t_ff_6_q[0]));  // open: Qn, reset, preset
  and BEQ (BEQ_out, OP[7], ~OP[6]);  // AND_Gate
  and RCb (RCb_out, t_ff_6_q[3], BEQ_out);
  or or_7 (or_7_out, t_ff_6_q[0], t_ff_6_q[1]);
  T_Flip_Flop #(.trigger("falling")) t_ff_7 (.T(or_7_out), .clk(CLK), .Q(t_ff_6_q[1]));  // open: Qn, reset, preset
  or or_8 (or_8_out, BEQ_out, BNQ_out, SUB_out, INP_out);
  // AND_Gate iA1 has open pins: in0=t_ff_6_q[0], in1=or_8_out, out=open
  // AND_Gate iA2 has open pins: in0=or_8_out, in1=t_ff_6_q[1], out=open
  or or_9 (or_9_out, t_ff_6_q[1], t_ff_6_q[2]);
  T_Flip_Flop #(.trigger("falling")) t_ff_8 (.T(or_9_out), .clk(CLK), .Q(t_ff_6_q[2]));  // open: Qn, reset, preset
  or or_10 (or_10_out, t_ff_6_q[2], t_ff_6_q[3]);
  T_Flip_Flop #(.trigger("falling")) t_ff_9 (.T(or_10_out), .clk(CLK), .Q(t_ff_6_q[3]));  // open: Qn, reset, preset
  and MATH (MATH_out, OP[5], ~OP[6], ~OP[7]);  // AND_Gate
  or ALU (ALU_out, MATH_out, OP[7]);
  and M_S (M_S_out, OP[4], MATH_out);
  or or_11 (ALU_ADD_SUB, M_S_out, OP[7]);
  assign ALU_CTRL = ALU_out ? t_ff_6_q : 4'bz;  // Controlled_Buffer controlled_buffer_1
  or or_12 (MAR_RW, IR_RW, IC_CTRL[1]);
  or or_13 (MAR_CS, IC_CTRL[1], RAM_SEND, IR_RW);
  or or_14 (MBR_CS, MBR_RW, IR_RW);
  or or_15 (IR_CS, IR_RW, t_ff_6_q[0], t_ff_6_q[1], t_ff_6_q[2], t_ff_6_q[3]);
  or or_16 (RAM_EXEC, iR2_out, IC_CTRL[2]);

  assign RAM_FETCH = MBR_RW;

  // Notes on the sheet:
  //   IC to MAR
  //   RAM - Read at MAR
  //   RAM Exec & IC ++
  //   RAM D to MBR
  //   Need Dx, Dy, MBR controls!
  //   MBR to IR AND MAR
  //   Main 1
  //   Main 2
  //   Main 3
  //   Main 4
  //   A3 is here
  //   OUT, EXEC, R_IN, L_IN
  //   INC, R, W
endmodule

module Binary_to_BCD (
  input  [7:0] BInaryInput,
  output [3:0] Binary1,
  output [3:0] Binary10,
  output [3:0] Binary100
);

  wire [2:0] add3_5_out_2;
  wire [3:0] add3_1_out_2, add3_2_out_2, add3_3_out_2, add3_4_out_2;

  Add3 add3_1 (.in_1({1'b0, BInaryInput[7:5]}), .out_2(add3_1_out_2));
  Add3 add3_2 (.in_1({add3_1_out_2[2:0], BInaryInput[4]}), .out_2(add3_2_out_2));
  Add3 add3_3 (.in_1({add3_2_out_2[2:0], BInaryInput[3]}), .out_2(add3_3_out_2));
  Add3 add3_4 (.in_1({add3_3_out_2[2:0], BInaryInput[2]}), .out_2(add3_4_out_2));
  Add3 add3_5 (.in_1({1'b0, add3_1_out_2[3], add3_2_out_2[3], add3_3_out_2[3]}), .out_2({Binary100[1], add3_5_out_2}));
  Add3 add3_6 (.in_1({add3_4_out_2[2:0], BInaryInput[1]}), .out_2({Binary10[0], Binary1[3:1]}));
  Add3 add3_7 (.in_1({add3_5_out_2, add3_4_out_2[3]}), .out_2({Binary100[0], Binary10[3:1]}));

  assign Binary1[0] = BInaryInput[0];
  assign Binary100[3:2] = 2'b00;
endmodule

module BCD_to_7Segment (
  input  [3:0] in_1,
  output [6:0] out_2
);

  wire and_1_out, and_2_out, and_3_out, and_4_out, and_5_out, and_6_out, and_7_out, and_8_out, and_9_out,
       and_10_out, and_11_out, and_12_out, and_14_out, not_1_out, not_2_out, not_3_out, not_4_out, or_1_out,
       or_2_out, or_3_out, xor_1_out, xor_2_out;

  not not_1 (not_1_out, in_1[3]);
  not not_2 (not_2_out, in_1[2]);
  not not_3 (not_3_out, in_1[1]);
  not not_4 (not_4_out, in_1[0]);
  and and_1 (and_1_out, in_1[0], not_3_out, not_2_out, not_1_out);
  and and_2 (and_2_out, not_4_out, not_3_out, in_1[2], not_1_out);
  and and_3 (and_3_out, in_1[2], not_1_out);
  xor xor_1 (xor_1_out, in_1[0], in_1[1]);
  nand nand_1 (out_2[4], not_4_out, in_1[1], not_2_out, not_1_out);
  xor xor_2 (xor_2_out, in_1[0], in_1[2]);
  and and_4 (and_4_out, xor_2_out, not_3_out);
  and and_5 (and_5_out, in_1[0], in_1[1], in_1[2]);
  and and_6 (and_6_out, in_1[1], not_2_out, not_1_out);
  and and_7 (and_7_out, in_1[1], in_1[2], not_1_out);
  or or_1 (or_1_out, and_6_out, and_7_out, and_8_out, and_9_out);
  and and_8 (and_8_out, not_3_out, not_2_out, in_1[3]);
  and and_9 (and_9_out, not_3_out, not_2_out, not_1_out);
  and and_10 (and_10_out, not_1_out, not_2_out);
  or or_2 (or_2_out, in_1[0], in_1[1]);
  and and_11 (and_11_out, in_1[0], in_1[1], in_1[2], not_1_out);
  and and_12 (and_12_out, not_3_out, not_2_out, not_1_out);
  and and_13 (out_2[2], ~and_1_out, ~and_2_out);  // AND_Gate
  nand nand_2 (out_2[3], and_3_out, xor_1_out);
  or or_3 (or_3_out, and_4_out, and_5_out);
  and and_14 (and_14_out, and_10_out, or_2_out);
  nand nand_3 (out_2[5], not_1_out, or_3_out);
  and and_15 (out_2[6], not_4_out, or_1_out);
  nor nor_1 (out_2[1], and_14_out, and_11_out);
  nor nor_2 (out_2[0], and_11_out, and_12_out);

  // Notes on the sheet:
  //   Segment order: GFABCDE
endmodule

module RAM_16x8 (
  input  CLK,
  input  Mode,
  input  [3:0] Address,
  input  [2:0] CPU_CTRL,
  input  [7:0] Data_in,
  output [7:0] Data_out
);

  wire and_1_out, controlled_buffer_1_out, d_ff_1_q, d_ff_1_qn, decoder_1_out0, decoder_1_out1,
       decoder_1_out2, decoder_1_out3, decoder_1_out4, decoder_1_out5, decoder_1_out6, decoder_1_out7,
       decoder_1_out8, decoder_1_out9, decoder_1_out10, decoder_1_out11, decoder_1_out12, decoder_1_out13,
       decoder_1_out14, decoder_1_out15, not_1_out, not_2_out, or_1_out;
  wire [3:0] nibble_reg_1_o;
  wire [7:0] D_o, demultiplexer_1_out0, multiplexer_1_out, R_0_o;

  Byte_Reg R_0 (.Chip_Select(decoder_1_out0), .I(demultiplexer_1_out0), .Clock(CLK), .O(R_0_o), .Mode_RW(d_ff_1_q));
  Byte_Reg R_4 (.Chip_Select(decoder_1_out4), .I(demultiplexer_1_out0), .Clock(CLK), .O(R_0_o), .Mode_RW(d_ff_1_q));
  Byte_Reg R_8 (.Chip_Select(decoder_1_out8), .I(demultiplexer_1_out0), .Clock(CLK), .O(R_0_o), .Mode_RW(d_ff_1_q));
  Byte_Reg R_12 (.Chip_Select(decoder_1_out12), .I(demultiplexer_1_out0), .Clock(CLK), .O(R_0_o), .Mode_RW(d_ff_1_q));
  // Probe on R_0_o
  Multiplexer #(.width(8), .enable("false")) multiplexer_1 (
    .in0(R_0_o), .in1(Data_in), .out(multiplexer_1_out), .sel(CPU_CTRL[0]));
  Byte_Reg R_1 (.Chip_Select(decoder_1_out1), .I(demultiplexer_1_out0), .Clock(CLK), .O(R_0_o), .Mode_RW(d_ff_1_q));
  Byte_Reg R_5 (.Chip_Select(decoder_1_out5), .I(demultiplexer_1_out0), .Clock(CLK), .O(R_0_o), .Mode_RW(d_ff_1_q));
  Byte_Reg R_9 (.Chip_Select(decoder_1_out9), .I(demultiplexer_1_out0), .Clock(CLK), .O(R_0_o), .Mode_RW(d_ff_1_q));
  Byte_Reg R_13 (.Chip_Select(decoder_1_out13), .I(demultiplexer_1_out0), .Clock(CLK), .O(R_0_o), .Mode_RW(d_ff_1_q));
  or or_1 (or_1_out, CPU_CTRL[0], and_1_out);
  // Probe on multiplexer_1_out
  not not_1 (not_1_out, not_2_out);
  not not_2 (not_2_out, CLK);
  Byte_Reg D (.Chip_Select(1'b1), .I(multiplexer_1_out), .Clock(not_1_out), .O(D_o), .Mode_RW(or_1_out));
  // Probe on D_o
  Byte_Reg R_2 (.Chip_Select(decoder_1_out2), .I(demultiplexer_1_out0), .Clock(CLK), .O(R_0_o), .Mode_RW(d_ff_1_q));
  Byte_Reg R_6 (.Chip_Select(decoder_1_out6), .I(demultiplexer_1_out0), .Clock(CLK), .O(R_0_o), .Mode_RW(d_ff_1_q));
  Byte_Reg R_10 (.Chip_Select(decoder_1_out10), .I(demultiplexer_1_out0), .Clock(CLK), .O(R_0_o), .Mode_RW(d_ff_1_q));
  Byte_Reg R_14 (.Chip_Select(decoder_1_out14), .I(demultiplexer_1_out0), .Clock(CLK), .O(R_0_o), .Mode_RW(d_ff_1_q));
  Demultiplexer #(.width(8), .enable("false")) demultiplexer_1 (
    .out0(demultiplexer_1_out0), .out1(Data_out), .in(D_o), .sel(CPU_CTRL[2]));
  Byte_Reg R_3 (.Chip_Select(decoder_1_out3), .I(demultiplexer_1_out0), .Clock(CLK), .O(R_0_o), .Mode_RW(d_ff_1_q));
  Byte_Reg R_7 (.Chip_Select(decoder_1_out7), .I(demultiplexer_1_out0), .Clock(CLK), .O(R_0_o), .Mode_RW(d_ff_1_q));
  Byte_Reg R_11 (.Chip_Select(decoder_1_out11), .I(demultiplexer_1_out0), .Clock(CLK), .O(R_0_o), .Mode_RW(d_ff_1_q));
  Byte_Reg R_15 (.Chip_Select(decoder_1_out15), .I(demultiplexer_1_out0), .Clock(CLK), .O(R_0_o), .Mode_RW(d_ff_1_q));
  Decoder #(.select(4), .enable("false")) decoder_1 (
    .out0(decoder_1_out0), .out1(decoder_1_out1), .out2(decoder_1_out2), .out3(decoder_1_out3),
    .out4(decoder_1_out4), .out5(decoder_1_out5), .out6(decoder_1_out6), .out7(decoder_1_out7),
    .out8(decoder_1_out8), .out9(decoder_1_out9), .out10(decoder_1_out10), .out11(decoder_1_out11),
    .out12(decoder_1_out12), .out13(decoder_1_out13), .out14(decoder_1_out14), .out15(decoder_1_out15),
    .sel(nibble_reg_1_o));
  and and_1 (and_1_out, CPU_CTRL[1], d_ff_1_qn);
  D_Flip_Flop d_ff_1 (.D(Mode), .clk(controlled_buffer_1_out), .Q(d_ff_1_q), .Qn(d_ff_1_qn));  // open: preset, reset
  assign controlled_buffer_1_out = CPU_CTRL[0] ? CLK : 1'bz;  // Controlled_Buffer controlled_buffer_1
  Nibble_Reg nibble_reg_1 (.O(nibble_reg_1_o), .Chip_Select(1'b1), .Mode_RW(CPU_CTRL[0]), .Clock(CLK), .I(Address));

  // Other names for the same wires on the sheet: SET = CPU_CTRL[0]; EXEC = CPU_CTRL[1]; FETCH = CPU_CTRL[2]

  // Notes on the sheet:
  //   FETCH, EXEC, SET
endmodule

module ALU (
  input  [3:0] CTRL,
  input  ADD_SUB,
  input  CLK,
  input  [7:0] L,
  input  [7:0] R,
  output [2:0] Status,
  output [7:0] A
);

  wire or_1_out, or_2_out, or_3_out, or_4_out;
  wire [3:0] undriven;
  wire [3:3] nibble_reg_1_o;
  wire [7:0] byte_reg_1_o, byte_reg_2_o, nor_1_out, S_out, xor_1_out;
  wire [7:1] Cout_out;
  wire [7:7] Cout_out_2;

  or or_1 (or_1_out, CTRL[2], CTRL[0]);
  or or_2 (or_2_out, CTRL[2], CTRL[1]);
  Byte_Reg byte_reg_1 (.Chip_Select(or_1_out), .I(L), .Clock(CLK), .O(byte_reg_1_o), .Mode_RW(CTRL[0]));
  Byte_Reg byte_reg_2 (.Chip_Select(or_2_out), .I(R), .Clock(CLK), .O(byte_reg_2_o), .Mode_RW(CTRL[1]));
  assign xor_1_out = {8{ADD_SUB}} ^ byte_reg_1_o;  // XOR_Gate xor_1, 8 bits wide
  assign S_out = xor_1_out ^ byte_reg_2_o ^ {Cout_out, ADD_SUB};  // XOR_Gate S, 8 bits wide
  NotExactlyOne Cout[7:0] (
    .out({Cout_out_2[7], Cout_out}), .in0(byte_reg_2_o), .in1(xor_1_out), .in2({Cout_out, ADD_SUB}),
    .in3(nor_1_out));
  assign nor_1_out = ~({Cout_out, ADD_SUB} | byte_reg_2_o | xor_1_out);  // NOR_Gate nor_1, 8 bits wide
  nor Zero (undriven[1], S_out[0], S_out[1], S_out[2], S_out[3], S_out[4], S_out[5], S_out[6], S_out[7]);
  or or_3 (or_3_out, CTRL[3], CTRL[2]);
  or or_4 (or_4_out, CTRL[3], CTRL[2]);
  Nibble_Reg nibble_reg_1 (
    .O({nibble_reg_1_o[3], Status}), .Chip_Select(or_3_out), .Mode_RW(CTRL[2]), .Clock(CLK),
    .I({undriven[3], Cout_out_2[7], undriven[1:0]}));
  Byte_Reg byte_reg_3 (.Chip_Select(or_4_out), .I(S_out), .Clock(CLK), .O(A), .Mode_RW(CTRL[2]));

  // Other names for the same wires on the sheet: L_IN = CTRL[0]; R_IN = CTRL[1]; EXEC = CTRL[2]; A_OUT = CTRL[3]

  // Notes on the sheet:
  //   ALU operations: Add, Sub, Compare = Sub
  //   OUT, EXEC, R_IN, L_IN
  //   Neg, Zero, OF
endmodule

module Byte_Reg (
  input  [7:0] I,
  input  Clock,
  input  Mode_RW,
  input  Chip_Select,
  output [7:0] O
);

  wire and_1_out, and_2_out, not_1_out, not_2_out;
  wire [7:0] controlled_buffer_1_out, R_0_q;

  not not_1 (not_1_out, Clock);
  assign controlled_buffer_1_out = and_1_out ? I : 8'bz;  // Controlled_Buffer controlled_buffer_1
  not not_2 (not_2_out, not_1_out);
  and and_1 (and_1_out, Mode_RW, Chip_Select);
  and and_2 (and_2_out, Chip_Select, ~Mode_RW);  // AND_Gate
  D_Flip_Flop R_4 (.D(controlled_buffer_1_out[4]), .clk(not_2_out), .Q(R_0_q[4]));  // open: Qn, preset, reset
  D_Flip_Flop R_5 (.D(controlled_buffer_1_out[5]), .clk(not_2_out), .Q(R_0_q[5]));  // open: Qn, preset, reset
  D_Flip_Flop R_6 (.D(controlled_buffer_1_out[6]), .clk(not_2_out), .Q(R_0_q[6]));  // open: Qn, preset, reset
  D_Flip_Flop R_7 (.D(controlled_buffer_1_out[7]), .clk(not_2_out), .Q(R_0_q[7]));  // open: Qn, preset, reset
  assign O = and_2_out ? R_0_q : 8'bz;  // Controlled_Buffer controlled_buffer_2
  D_Flip_Flop R_0 (.D(controlled_buffer_1_out[0]), .clk(not_2_out), .Q(R_0_q[0]));  // open: Qn, preset, reset
  D_Flip_Flop R_1 (.D(controlled_buffer_1_out[1]), .clk(not_2_out), .Q(R_0_q[1]));  // open: Qn, preset, reset
  D_Flip_Flop R_2 (.D(controlled_buffer_1_out[2]), .clk(not_2_out), .Q(R_0_q[2]));  // open: Qn, preset, reset
  D_Flip_Flop R_3 (.D(controlled_buffer_1_out[3]), .clk(not_2_out), .Q(R_0_q[3]));  // open: Qn, preset, reset
endmodule

module Nibble_Reg (
  input  [3:0] I,
  input  Clock,
  input  Mode_RW,
  input  Chip_Select,
  output [3:0] O
);

  wire and_1_out, and_2_out, not_1_out, not_2_out;
  wire [3:0] controlled_buffer_1_out, d_ff_1_q;

  not not_1 (not_1_out, Clock);
  assign controlled_buffer_1_out = and_1_out ? I : 4'bz;  // Controlled_Buffer controlled_buffer_1
  not not_2 (not_2_out, not_1_out);
  and and_1 (and_1_out, Mode_RW, Chip_Select);
  and and_2 (and_2_out, Chip_Select, ~Mode_RW);  // AND_Gate
  D_Flip_Flop d_ff_1 (.D(controlled_buffer_1_out[0]), .clk(not_2_out), .Q(d_ff_1_q[0]));  // open: Qn, preset, reset
  D_Flip_Flop d_ff_2 (.D(controlled_buffer_1_out[1]), .clk(not_2_out), .Q(d_ff_1_q[1]));  // open: Qn, preset, reset
  D_Flip_Flop d_ff_3 (.D(controlled_buffer_1_out[2]), .clk(not_2_out), .Q(d_ff_1_q[2]));  // open: Qn, preset, reset
  D_Flip_Flop d_ff_4 (.D(controlled_buffer_1_out[3]), .clk(not_2_out), .Q(d_ff_1_q[3]));  // open: Qn, preset, reset
  assign O = and_2_out ? d_ff_1_q : 4'bz;  // Controlled_Buffer controlled_buffer_2
endmodule

module Nibble_Counter (
  input  [3:0] I,
  input  Write_Enable,
  input  Increment,
  input  Read_Enable,
  input  Clock,
  output [3:0] O
);

  wire and_1_out, and_2_out, and_3_out, or_1_out, or_2_out, or_3_out, or_4_out, or_5_out, or_6_out, or_7_out,
       or_8_out;
  wire [3:0] controlled_buffer_1_out, j_k_ff_1_q;

  assign controlled_buffer_1_out = Write_Enable ? I : 4'bz;  // Controlled_Buffer controlled_buffer_1
  or or_1 (or_1_out, controlled_buffer_1_out[0], Increment);
  or or_2 (or_2_out, Increment, ~controlled_buffer_1_out[0]);  // OR_Gate
  and and_1 (and_1_out, j_k_ff_1_q[0], Increment);
  J_K_Flip_Flop j_k_ff_1 (.J(or_1_out), .K(or_2_out), .clk(Clock), .Q(j_k_ff_1_q[0]));  // open: Qn, preset, reset
  J_K_Flip_Flop j_k_ff_2 (.J(or_3_out), .K(or_4_out), .clk(Clock), .Q(j_k_ff_1_q[1]));  // open: Qn, preset, reset
  or or_3 (or_3_out, controlled_buffer_1_out[1], and_1_out);
  or or_4 (or_4_out, and_1_out, ~controlled_buffer_1_out[1]);  // OR_Gate
  and and_2 (and_2_out, j_k_ff_1_q[1], j_k_ff_1_q[0], Increment);
  or or_5 (or_5_out, controlled_buffer_1_out[2], and_2_out);
  or or_6 (or_6_out, and_2_out, ~controlled_buffer_1_out[2]);  // OR_Gate
  J_K_Flip_Flop j_k_ff_3 (.J(or_5_out), .K(or_6_out), .clk(Clock), .Q(j_k_ff_1_q[2]));  // open: Qn, preset, reset
  and and_3 (and_3_out, j_k_ff_1_q[2], j_k_ff_1_q[1], j_k_ff_1_q[0], Increment);
  J_K_Flip_Flop j_k_ff_4 (.J(or_7_out), .K(or_8_out), .clk(Clock), .Q(j_k_ff_1_q[3]));  // open: Qn, preset, reset
  or or_7 (or_7_out, controlled_buffer_1_out[3], and_3_out);
  or or_8 (or_8_out, and_3_out, ~controlled_buffer_1_out[3]);  // OR_Gate
  assign O = Read_Enable ? j_k_ff_1_q : 4'bz;  // Controlled_Buffer controlled_buffer_2
endmodule

module Bit_Adder (
  input  Cin,
  input  X,
  input  Y,
  output Sum,
  output Cout
);

  wire and_1_out, and_2_out, xor_1_out;

  and and_1 (and_1_out, Y, X);
  or or_1 (Cout, and_1_out, and_2_out);
  xor xor_1 (xor_1_out, X, Y);
  and and_2 (and_2_out, xor_1_out, Cin);
  xor xor_2 (Sum, Cin, xor_1_out);
endmodule

module Add3 (
  input  [3:0] in_1,
  output [3:0] out_2
);

  wire and_1_out, and_2_out, and_3_out, and_4_out, and_5_out, and_6_out, and_7_out, and_8_out, and_9_out,
       bit_adder_1_cout, bit_adder_1_sum, bit_adder_2_cout, bit_adder_2_sum, bit_adder_3_cout,
       bit_adder_3_sum, bit_adder_4_sum, or_1_out, or_2_out;

  or or_1 (or_1_out, in_1[0], in_1[1]);
  and and_1 (and_1_out, or_1_out, in_1[2]);
  Bit_Adder bit_adder_1 (.Cout(bit_adder_1_cout), .Sum(bit_adder_1_sum), .Y(1'b1), .X(in_1[0]));  // open: Cin
  Bit_Adder bit_adder_2 (.Cout(bit_adder_2_cout), .Sum(bit_adder_2_sum), .Y(1'b1), .X(in_1[1]), .Cin(bit_adder_1_cout));
  Bit_Adder bit_adder_3 (.Cout(bit_adder_3_cout), .Sum(bit_adder_3_sum), .Y(1'b0), .X(in_1[2]), .Cin(bit_adder_2_cout));
  Bit_Adder bit_adder_4 (.Sum(bit_adder_4_sum), .Y(1'b0), .X(in_1[3]), .Cin(bit_adder_3_cout));  // open: Cout
  or or_2 (or_2_out, in_1[3], and_1_out);
  and and_2 (and_2_out, or_2_out, bit_adder_1_sum);
  and and_3 (and_3_out, ~or_2_out, in_1[0]);  // AND_Gate
  and and_4 (and_4_out, or_2_out, bit_adder_2_sum);
  and and_5 (and_5_out, ~or_2_out, in_1[1]);  // AND_Gate
  and and_6 (and_6_out, or_2_out, bit_adder_3_sum);
  and and_7 (and_7_out, ~or_2_out, in_1[2]);  // AND_Gate
  and and_8 (and_8_out, or_2_out, bit_adder_4_sum);
  and and_9 (and_9_out, ~or_2_out, in_1[3]);  // AND_Gate
  or or_3 (out_2[0], and_2_out, and_3_out);
  or or_4 (out_2[1], and_4_out, and_5_out);
  or or_5 (out_2[2], and_6_out, and_7_out);
  or or_6 (out_2[3], and_8_out, and_9_out);
endmodule
